# Fritzing sketch car-sunlight-sensor (saved by Fritzing 0.9.3b)
breadboards: 1

parts:
  Part1 = PWM Shield
  LCD1 = LCD screen
  R1 = Photocell (LDR) [package=THT]
  R2 = Resistor [tolerance=±5% resistance=220 package=THT]
  R3 = TRIMPOT [package=trimpot_pth_s3_lock]

nets:
  N1: Part1.XLAT, Part1.XLAT_-_D9, LCD1.DB6
  N2: Part1.BLANK, Part1.BLANK_-_D10, LCD1.DB5
  N3: Part1.SCLK, Part1.SCLK_-_D13, LCD1.RS
  N4: Part1.5V_A, LCD1.VDD, R1.pin_1, R3.CCW
  N5: Part1.A0, R1.pin_0, R2.Pin_0
  N6: Part1.D8, LCD1.DB7
  N7: Part1.SIN_-_D11, LCD1.DB4
  N8: Part1.D12, LCD1.E
  N9: Part1.GND_-_GND@0, LCD1.VSS, LCD1.R/W, LCD1.LED+, LCD1.LED-, R2.Pin_1, R3.CW
  N10: LCD1.V0, R3.WIPER
